# Fritzing sketch SaoJoseRelogio (saved by Fritzing 0.9.3b)
breadboards: 1

parts:
  Componente2 = Arduino Nano (Rev3.0)
  Pulsos = smd LED [color="Red (633nm)" package="0603 [SMD]"]
  R1 = Resistor [tolerance=±5% resistance=220 package="0603 [SMD]"]
  R2 = Resistor [tolerance=±5% resistance=220 package="2010 [SMD]"]
  R3 = Resistor [tolerance=±5% resistance=220 package="2010 [SMD]"]
  Power_5V = Power plug
  Modo = LED - 5mm [color="Red (633nm)" package="5 mm [THT]"]
  Sentido = LED - 5mm [color="Red (633nm)" package="5 mm [THT]"]
  Ajuste_Horário = Round Pushbutton
  Ajuste_Anti-horário = Round Pushbutton
  ENA = Screw terminal - 2 pins [package=THT]
  DIR = Screw terminal - 2 pins [package=THT]
  PUL = Screw terminal - 2 pins [package=THT]

nets:
  GND: Componente2.GND, R1.Pin_1, R2.Pin_1, R3.Pin_1, Power_5V.GND, Ajuste_Horário.leg0, Ajuste_Anti-horário.leg1, ENA.pin2, DIR.pin2, PUL.pin2
  N1: Componente2.D2, ENA.pin1
  N2: Componente2.D3, DIR.pin1
  N3: Componente2.D4, PUL.pin1
  N4: Componente2.D5, Ajuste_Anti-horário.leg0
  N5: Componente2.D6, Ajuste_Horário.leg1
  5V: Componente2.5V, Power_5V.VCC
  N6: Componente2.A1, Sentido.anode
  N7: Componente2.A0, Modo.anode
  N8: Componente2.D13/SCK, Pulsos.anode
  N9: Pulsos.cathode, R1.Pin_0
  N10: R2.Pin_0, Modo.cathode
  N11: R3.Pin_0, Sentido.cathode
